# Fritzing sketch PCB_PCF8574 (saved by Fritzing 0.9.3b)
circuit board: 2.24825cm x 3.65727cm
breadboards: 1

parts:
  S1 = Toggle Switch [package=THT]
  S2 = Toggle Switch [package=THT]
  S3 = Toggle Switch [package=THT]
  U1 = PCF8574 [package="DIP16 [THT]"]

nets:
  5V: S1.L1, S2.L1, S3.L1, U1.VCC
  N1: S1.COM, U1.A2
  GND: S1.L2, S2.L2, S3.L2, U1.GND
  N2: S2.COM, U1.A1
  N3: S3.COM, U1.A0

notes:
  VCC GND
  PCF8574
