# Fritzing sketch PCB_PCF8574_03 (saved by Fritzing 0.9.3b)
circuit board: 3.31283cm x 4.44148cm
breadboards: 1

parts:
  Componente1 = Arduino Uno (Rev3)
  INT_SDA_SCL = female pin header, 3 pins [form="♀ (female)"]
  P4-P7 = female pin header, 4 pins [form="♀ (female)"]
  P0-P3 = female pin header, 4 pins [form="♀ (female)"]
  Pull-upp_SCL = Resistor [tolerance=±5% resistance=10k package=THT]
  Pull-up_SDA = Resistor [tolerance=±5% resistance=10k package=THT]
  Pull-up_int = Resistor [tolerance=±5% resistance=10k package=THT]
  Adress_i2c = DIP SWITCH [package=dipswitch-02]
  SW2 = DIP SWITCH [package=dipswitch-02]
  Pull-down_res_A0 = Resistor [tolerance=±5% resistance=10k package=THT]
  Pull-down_res_A1 = Resistor [tolerance=±5% resistance=10k package=THT]
  Pull-down_res_A2 = Resistor [tolerance=±5% resistance=10k package=THT]
  Power_from_controller = female pin header, 2 pins [form="♀ (female)"]
  U1 = PCF8574 [package="DIP16 [THT]"]

nets:
  N1: Componente1.A4/SDA, INT_SDA_SCL.pin3, Pull-upp_SCL.Pin_0, U1.SDA
  N2: Componente1.A5/SCL, INT_SDA_SCL.pin2, Pull-up_SDA.Pin_0, U1.SCL
  GND: Componente1.GND, Pull-down_res_A0.Pin_1, Pull-down_res_A1.Pin_1, Pull-down_res_A2.Pin_1, Power_from_controller.pin1, U1.GND
  N3: Componente1.D2, INT_SDA_SCL.pin1, Pull-up_int.Pin_0, U1.INT
  5V: Componente1.5V, Pull-upp_SCL.Pin_1, Pull-up_SDA.Pin_1, Pull-up_int.Pin_1, Adress_i2c.3, Adress_i2c.4, SW2.3, SW2.4, Power_from_controller.pin2, U1.VCC
  N4: P4-P7.pin1, U1.P4
  N5: P4-P7.pin2, U1.P5
  N6: P4-P7.pin3, U1.P6
  N7: P4-P7.pin4, U1.P7
  N8: P0-P3.pin1, U1.P3
  N9: P0-P3.pin2, U1.P2
  N10: P0-P3.pin3, U1.P1
  N11: P0-P3.pin4, U1.P0
  N12: Adress_i2c.1, Pull-down_res_A0.Pin_0, U1.A0
  N13: Adress_i2c.2, SW2.1, Pull-down_res_A1.Pin_0, U1.A1
  N14: SW2.2, Pull-down_res_A2.Pin_0, U1.A2

notes:
  VG
  PCF8574
  Reef
