# Fritzing sketch testReadWriteLedButton (saved by Fritzing 0.9.3b)
breadboards: 1

parts:
  Componente1 = Arduino Uno (Rev3)
  U1 = PCF8574 [package="DIP16 [THT]"]
  S2 = Pushbutton [package="[THT]"]
  R2 = Resistor [tolerance=±5% resistance=10k package=THT]
  LED3 = LED - 5mm [color="Red (633nm)" package="5 mm [THT]"]
  R8 = Resistor [tolerance=±5% resistance=220 package=THT]
  R9 = Resistor [tolerance=±5% resistance=10k package=THT]
  R10 = Resistor [tolerance=±5% resistance=10k package=THT]
  R11 = Resistor [tolerance=±5% resistance=10k package=THT]

nets:
  N1: Componente1.A4/SDA, U1.SDA, R10.Pin_1
  N2: Componente1.A5/SCL, U1.SCL, R9.Pin_1
  GND: Componente1.GND, U1.A1, U1.A3, U1.GND, R2.Pin_1, R8.Pin_1
  N3: Componente1.D2, U1.INT, R11.Pin_1
  5V: Componente1.5V, U1.A0, U1.VCC, S2.Pin_1, S2.Pin_2, R9.Pin_0, R10.Pin_0, R11.Pin_0
  N4: U1.P0, S2.Pin_3, S2.Pin_4, R2.Pin_0
  N5: U1.P1, LED3.cathode
  N6: LED3.anode, R8.Pin_0
